# Fritzing sketch looper (saved by Fritzing 0.8.7b)
stripboards: 2

parts:
  R1 = Resistor [tolerance=±5% resistance=220 package=THT]
  LED1 = LED - 5mm [color="Red (633nm)" package="5 mm [THT]"]
  LED2 = LED - 5mm [color="Red (633nm)" package="5 mm [THT]"]
  R2 = Resistor [tolerance=±5% resistance=220 package=THT]
  R3 = Resistor [tolerance=±5% resistance=220 package=THT]
  LED3 = LED - 5mm [color="Red (633nm)" package="5 mm [THT]"]
  LED4 = LED - 5mm [color="Red (633nm)" package="5 mm [THT]"]
  R4 = Resistor [tolerance=±5% resistance=220 package=THT]
  LED5 = LED - 5mm [color="Red (633nm)" package="5 mm [THT]"]
  R5 = Resistor [tolerance=±5% package="2512 [SMD]"]
  R5_2 = Resistor [tolerance=±5% package="2010 [SMD]"]
  LED6 = LED - 5mm [color="Red (633nm)" package="5 mm [THT]"]
  R6 = Resistor [tolerance=±5% package="2010 [SMD]"]
  R7 = Resistor [tolerance=±5% resistance=220 package=THT]
  S1 = Pushbutton [package="[THT]"]
  R8 = Resistor [tolerance=±5% resistance=220 package=THT]
  R9 = Resistor [tolerance=±5% resistance=220 package=THT]
  R10 = Resistor [tolerance=±5% resistance=220 package=THT]
  S2 = Pushbutton [package="[THT]"]
  S3 = Pushbutton [package="[THT]"]
  S4 = Pushbutton [package="[THT]"]
  Part1 = Variable Capacitor [capacitance=100nF max_capacitance=10pF min_capacitance=2pF voltage=35V]
  Part2 = Variable Capacitor [capacitance=100nF max_capacitance=10pF min_capacitance=2pF voltage=35V]
  Part3 = Variable Capacitor [capacitance=100nF max_capacitance=10pF min_capacitance=2pF voltage=35V]
  Part4 = Variable Capacitor [capacitance=100nF max_capacitance=10pF min_capacitance=2pF voltage=35V]

nets:
  N1: R1.Pin_0, LED1.anode
  N2: LED1.cathode, LED2.cathode, LED3.cathode, LED4.cathode, LED5.cathode, LED6.cathode
  N3: LED2.anode, R2.Pin_0
  N4: R3.Pin_0, LED3.anode
  N5: LED4.anode, R4.Pin_0
  N6: LED5.anode, R5.Pin_0, R5_2.Pin_0
  N7: R5.Pin_1, R5_2.Pin_1
  N8: LED6.anode, R6.Pin_0
  N9: R7.Pin_0, S4.Pin_3, S4.Pin_4
  N10: R7.Pin_1, R8.Pin_1, R9.Pin_1, R10.Pin_1
  N11: S1.Pin_1, S1.Pin_2, S2.Pin_2, S3.Pin_2, S4.Pin_2
  N12: S1.Pin_3, S1.Pin_4, R10.Pin_0
  N13: R8.Pin_0, S3.Pin_3, S3.Pin_4
  N14: R9.Pin_0, S2.Pin_3, S2.Pin_4
  N15: Part1.1, Part2.1, Part3.1, Part4.1
  N16: Part1.2, Part2.2, Part3.2, Part4.2
